// Logisim project computer.circ as structural Verilog
module cpu (
  input  in_1,
  input  RESET
);

  wire AMA_RESET, AMA_WRITE, and_1_out, clk_1_clock_out, clock_1_out, demultiplexer_1_out1,
       INSTRUCT_REG_WRITE, IO_SELECT_REG_WRITE, JUMP, LOAD_KEYBOARD, MAR_0_WRITE, MAR_1_WRITE, MAR_2_WRITE,
       MAR_3_WRITE, MAR_READ, not_1_out, or_1_out, or_2_out, or_3_out, or_4_out, OUTPUT_HIGH_WRITE,
       OUTPUT_LOW_WRITE, PC_ENB, PC_OUT, RAM_READ, RAM_WRITE, READ_8_BIT_OUTPUT, READ_KEYBOARD,
       REGFILE_TO_BUS, REGFILE_WRITE, RMA_RESET, RMA_WRITE, STEP_RESET;
  wire [1:0] multiplexer_1_out;
  wire [2:0] keyboard_1_data_2;
  wire [3:0] alu_1_data_out, alu_1_flag_out, alu_memory_access_1_data_out, controlled_buffer_1_out,
       instruction_register_1_always_out, io_selection_register_1_always_out, keyboard_1_data,
       multiplexer_2_out, pull_resistor_4_node, pull_resistor_8_node, pull_resistor_12_node,
       pull_resistor_16_node, ram_1_dout, register_file_1_data_out_a, register_file_1_data_out_b,
       register_file_1_flag_out, register_memory_access_1_data_out, step_counter_1_data_out;
  wire [7:0] io_register_1_data_out;
  wire [15:0] program_counter_1_always_out;

  Clock clock_1 (.out(clock_1_out));
  clk clk_1 (.CLOCK_IN(clock_1_out), .CLOCK_ENABLE(in_1), .CLOCK_OUT(clk_1_clock_out));  // open: MANUAL_TICK, HALT
  Hex_Digit_Display hex_digit_display_1 (.value(pull_resistor_4_node));  // open: dp
  LED led_1 (.in(pull_resistor_4_node[3]));
  LED led_2 (.in(pull_resistor_4_node[2]));
  LED led_3 (.in(pull_resistor_4_node[1]));
  LED led_4 (.in(pull_resistor_4_node[0]));
  Pull_Resistor pull_resistor_1 (.node(pull_resistor_4_node[3]));
  Pull_Resistor pull_resistor_2 (.node(pull_resistor_4_node[2]));
  Pull_Resistor pull_resistor_3 (.node(pull_resistor_4_node[1]));
  Pull_Resistor pull_resistor_4 (.node(pull_resistor_4_node[0]));
  LED led_5 (.in(pull_resistor_8_node[3]));
  LED led_6 (.in(pull_resistor_8_node[2]));
  Pull_Resistor pull_resistor_5 (.node(pull_resistor_8_node[3]));
  Pull_Resistor pull_resistor_6 (.node(pull_resistor_8_node[2]));
  Hex_Digit_Display hex_digit_display_2 (.value(pull_resistor_8_node));  // open: dp
  LED led_7 (.in(pull_resistor_8_node[1]));
  LED led_8 (.in(pull_resistor_8_node[0]));
  LED led_9 (.in(pull_resistor_12_node[3]));
  Pull_Resistor pull_resistor_7 (.node(pull_resistor_8_node[1]));
  Pull_Resistor pull_resistor_8 (.node(pull_resistor_8_node[0]));
  Pull_Resistor pull_resistor_9 (.node(pull_resistor_12_node[3]));
  Hex_Digit_Display hex_digit_display_3 (.value(pull_resistor_12_node));  // open: dp
  LED led_10 (.in(pull_resistor_12_node[2]));
  LED led_11 (.in(pull_resistor_12_node[1]));
  LED led_12 (.in(pull_resistor_12_node[0]));
  Pull_Resistor pull_resistor_10 (.node(pull_resistor_12_node[2]));
  Pull_Resistor pull_resistor_11 (.node(pull_resistor_12_node[1]));
  Pull_Resistor pull_resistor_12 (.node(pull_resistor_12_node[0]));
  Hex_Digit_Display hex_digit_display_4 (.value(pull_resistor_16_node));  // open: dp
  LED led_13 (.in(pull_resistor_16_node[3]));
  LED led_14 (.in(pull_resistor_16_node[2]));
  LED led_15 (.in(pull_resistor_16_node[1]));
  Pull_Resistor pull_resistor_13 (.node(pull_resistor_16_node[3]));
  Pull_Resistor pull_resistor_14 (.node(pull_resistor_16_node[2]));
  Pull_Resistor pull_resistor_15 (.node(pull_resistor_16_node[1]));
  LED led_16 (.in(pull_resistor_16_node[0]));
  LED led_17 (.in(program_counter_1_always_out[15]));
  Pull_Resistor pull_resistor_16 (.node(pull_resistor_16_node[0]));
  LED led_18 (.in(program_counter_1_always_out[14]));
  LED led_19 (.in(program_counter_1_always_out[13]));
  LED led_20 (.in(program_counter_1_always_out[12]));
  LED led_21 (.in(program_counter_1_always_out[11]));
  LED led_22 (.in(program_counter_1_always_out[10]));
  LED led_23 (.in(program_counter_1_always_out[9]));
  LED led_24 (.in(program_counter_1_always_out[8]));
  LED led_25 (.in(program_counter_1_always_out[7]));
  io_selection_register io_selection_register_1 (
    .DATA_IN(controlled_buffer_1_out), .WRITE(IO_SELECT_REG_WRITE), .CLOCK(clk_1_clock_out), .RESET(RESET),
    .ALWAYS_OUT(io_selection_register_1_always_out));  // open: READ, DATA_OUT
  LED led_26 (.in(program_counter_1_always_out[4]));
  LED led_27 (.in(program_counter_1_always_out[3]));
  LED led_28 (.in(program_counter_1_always_out[6]));
  LED led_29 (.in(program_counter_1_always_out[5]));
  RAM #(.addrWidth(16), .dataWidth(4), .enables("line")) ram_1 (
    .addr({pull_resistor_4_node, pull_resistor_8_node, pull_resistor_12_node, pull_resistor_16_node}),
    .we(RAM_WRITE), .clk(clk_1_clock_out), .din(controlled_buffer_1_out), .dout(ram_1_dout));
  LED led_30 (.in(program_counter_1_always_out[2]));
  LED led_31 (.in(program_counter_1_always_out[1]));
  LED led_32 (.in(program_counter_1_always_out[0]));
  program_counter program_counter_1 (
    .COUNTER_OUT(PC_OUT), .RESET(RESET), .JUMP(JUMP), .COUNTER_ENABLE(PC_ENB), .CLOCK(clk_1_clock_out),
    .ADDRESS_IN({pull_resistor_4_node, pull_resistor_8_node, pull_resistor_12_node, pull_resistor_16_node}),
    .ALWAYS_OUT(program_counter_1_always_out),
    .ADDRESS_OUT({pull_resistor_4_node, pull_resistor_8_node, pull_resistor_12_node, pull_resistor_16_node}));
  memory_address_register memory_address_register_1 (
    .DATA_IN(controlled_buffer_1_out), .MAR_WRITE({MAR_3_WRITE, MAR_2_WRITE, MAR_1_WRITE, MAR_0_WRITE}),
    .CLOCK(clk_1_clock_out), .RESET(RESET), .MAR_OUT(MAR_READ),
    .DATA_OUT({pull_resistor_4_node, pull_resistor_8_node, pull_resistor_12_node, pull_resistor_16_node}));
  io_register io_register_1 (
    .READ(READ_8_BIT_OUTPUT), .CLOCK(clk_1_clock_out), .RESET(RESET), .WRITE_LOW(OUTPUT_LOW_WRITE),
    .WRITE_HIGH(OUTPUT_HIGH_WRITE), .DATA_IN(controlled_buffer_1_out), .DATA_OUT(io_register_1_data_out));  // open: ALWAYS_OUT
  assign controlled_buffer_1_out = RAM_READ ? ram_1_dout : 4'bz;  // Controlled_Buffer controlled_buffer_1
  Demultiplexer #(.select(4)) demultiplexer_1 (
    .out1(demultiplexer_1_out1), .in(READ_8_BIT_OUTPUT), .sel(io_selection_register_1_always_out));  // open: out0, out2, out3, out4, out5, out6, out7, out8, out9, out10, out11, out12, out13, out14, out15
  LED led_33 (.in(controlled_buffer_1_out[3]));
  LED led_34 (.in(controlled_buffer_1_out[2]));
  LED led_35 (.in(controlled_buffer_1_out[1]));
  Pull_Resistor pull_resistor_17 (.node(controlled_buffer_1_out[3]));
  Pull_Resistor pull_resistor_18 (.node(controlled_buffer_1_out[2]));
  Pull_Resistor pull_resistor_19 (.node(controlled_buffer_1_out[1]));
  LED led_36 (.in(io_register_1_data_out[7]));
  Pull_Resistor pull_resistor_20 (.node(io_register_1_data_out[7]));
  LED led_37 (.in(controlled_buffer_1_out[0]));
  Pull_Resistor pull_resistor_21 (.node(controlled_buffer_1_out[0]));
  Hex_Digit_Display hex_digit_display_5 (.value(io_register_1_data_out[7:4]));  // open: dp
  LED led_38 (.in(io_register_1_data_out[6]));
  LED led_39 (.in(io_register_1_data_out[5]));
  LED led_40 (.in(io_register_1_data_out[4]));
  Pull_Resistor pull_resistor_22 (.node(io_register_1_data_out[6]));
  Pull_Resistor pull_resistor_23 (.node(io_register_1_data_out[5]));
  Pull_Resistor pull_resistor_24 (.node(io_register_1_data_out[4]));
  or or_1 (or_1_out, RESET, RMA_RESET);
  or or_2 (or_2_out, RESET, AMA_RESET);
  Hex_Digit_Display hex_digit_display_6 (.value(io_register_1_data_out[3:0]));  // open: dp
  LED led_41 (.in(io_register_1_data_out[3]));
  LED led_42 (.in(io_register_1_data_out[2]));
  LED led_43 (.in(io_register_1_data_out[1]));
  LED led_44 (.in(io_register_1_data_out[0]));
  Pull_Resistor pull_resistor_25 (.node(io_register_1_data_out[3]));
  Pull_Resistor pull_resistor_26 (.node(io_register_1_data_out[2]));
  Pull_Resistor pull_resistor_27 (.node(io_register_1_data_out[1]));
  Pull_Resistor pull_resistor_28 (.node(io_register_1_data_out[0]));
  register_memory_access register_memory_access_1 (
    .DATA_IN(controlled_buffer_1_out), .WRITE(RMA_WRITE), .CLOCK(clk_1_clock_out), .RESET(or_1_out),
    .DATA_OUT(register_memory_access_1_data_out));
  alu_memory_access alu_memory_access_1 (
    .DATA_IN(controlled_buffer_1_out), .WRITE(AMA_WRITE), .CLOCK(clk_1_clock_out), .RESET(or_2_out),
    .DATA_OUT(alu_memory_access_1_data_out));
  instruction_register instruction_register_1 (
    .DATA_IN(controlled_buffer_1_out), .WRITE(INSTRUCT_REG_WRITE), .CLOCK(clk_1_clock_out), .RESET(RESET),
    .ALWAYS_OUT(instruction_register_1_always_out));  // open: READ, DATA_OUT
  or or_3 (or_3_out, STEP_RESET, RESET);
  not not_1 (not_1_out, clk_1_clock_out);
  and and_1 (and_1_out, not_1_out, 1'b1);
  or or_4 (or_4_out, alu_memory_access_1_data_out[3], alu_memory_access_1_data_out[2]);
  assign controlled_buffer_1_out = REGFILE_TO_BUS ? register_file_1_data_out_b : 4'bz;  // Controlled_Buffer controlled_buffer_2
  Multiplexer #(.width(2)) multiplexer_1 (
    .in0(register_memory_access_1_data_out[3:2]), .in1(alu_memory_access_1_data_out[1:0]),
    .out(multiplexer_1_out), .sel(or_4_out));
  step_counter step_counter_1 (.RESET(or_3_out), .CLOCK(and_1_out), .DATA_OUT(step_counter_1_data_out));
  assign controlled_buffer_1_out = READ_KEYBOARD ? keyboard_1_data : 4'bz;  // Controlled_Buffer controlled_buffer_3
  Hex_Digit_Display hex_digit_display_7 (.value(step_counter_1_data_out));  // open: dp
  TTY #(.cols(60), .rows(15)) tty_1 (
    .data(io_register_1_data_out[6:0]), .clk(clk_1_clock_out), .we(demultiplexer_1_out1), .clr(RESET));
  Keyboard keyboard_1 (
    .clk(LOAD_KEYBOARD), .clr(RESET), .data({keyboard_1_data_2, keyboard_1_data}));  // open: re, avail
  alu alu_1 (
    .ENABLE(or_4_out), .SELECT_OP(alu_memory_access_1_data_out[3:2]), .A_IN(register_file_1_data_out_a),
    .B_IN(register_file_1_data_out_b), .DATA_OUT(alu_1_data_out), .FLAG_OUT(alu_1_flag_out));  // open: BORROW_IN, CARRY_IN, BORROW_OUT
  Multiplexer #(.width(4)) multiplexer_2 (
    .in0(controlled_buffer_1_out), .in1(alu_1_data_out), .out(multiplexer_2_out), .sel(or_4_out));
  control_unit_2 control_unit_2_1 (
    .FLAG(register_file_1_flag_out), .FROM_RAM(controlled_buffer_1_out), .CLOCK(clk_1_clock_out),
    .STEP(step_counter_1_data_out), .INSTRUCTION(instruction_register_1_always_out), .RAM_READ(RAM_READ),
    .REGFILE_READ(REGFILE_TO_BUS), .MAR_READ(MAR_READ), .IO_READ(READ_8_BIT_OUTPUT),
    .KEYBOARD_READ(READ_KEYBOARD), .INSTRUSTION_REG_WRITE(INSTRUCT_REG_WRITE), .RMA_WRITE(RMA_WRITE),
    .AMA_WRITE(AMA_WRITE), .REGFILE_WRITE(REGFILE_WRITE), .RAM_WRITE(RAM_WRITE),
    .IO_WRITE(IO_SELECT_REG_WRITE), .KEYBOARD_WRITE(LOAD_KEYBOARD), .NIBLE_HIGH_WRITE(OUTPUT_HIGH_WRITE),
    .NIBLE_LOW_WRITE(OUTPUT_LOW_WRITE), .PC_ENABLE(PC_ENB), .PC_OUT_DISABLE(PC_OUT),
    .STEP_COUNTER_RESET(STEP_RESET), .RMA_RESET(RMA_RESET), .AMA_RESET(AMA_RESET), .MAR_3(MAR_3_WRITE),
    .MAR_2(MAR_2_WRITE), .MAR_1(MAR_1_WRITE), .MAR_0(MAR_0_WRITE), .JUMP_ENABLE(JUMP));
  register_file register_file_1 (
    .FLAG_CHECK(or_4_out), .CLOCK(clk_1_clock_out), .RESET(RESET), .WRITE_ENABLE(REGFILE_WRITE),
    .FLAG_IN(alu_1_flag_out), .WRITE(multiplexer_1_out), .SELECT_A(register_memory_access_1_data_out[3:2]),
    .SELECT_B(register_memory_access_1_data_out[1:0]), .DATA_IN(multiplexer_2_out),
    .DATA_OUT_A(register_file_1_data_out_a), .DATA_OUT_B(register_file_1_data_out_b),
    .FLAG_OUT(register_file_1_flag_out));

  // Notes on the sheet:
  //   ADDRESS BUS
  //   DATA BUS
endmodule

module clk (
  input  CLOCK_IN,
  input  CLOCK_ENABLE,
  input  MANUAL_TICK,
  input  HALT,
  output CLOCK_OUT
);

  wire and_1_out, and_2_out, not_1_out, not_2_out, or_1_out;

  not not_1 (not_1_out, CLOCK_ENABLE);
  and and_1 (and_1_out, CLOCK_IN, CLOCK_ENABLE);
  and and_2 (and_2_out, not_1_out, MANUAL_TICK);
  or or_1 (or_1_out, and_1_out, and_2_out);
  not not_2 (not_2_out, HALT);
  and and_3 (CLOCK_OUT, or_1_out, not_2_out);
endmodule

module program_counter (
  input  RESET,
  input  JUMP,
  input  COUNTER_ENABLE,
  input  CLOCK,
  input  [15:0] ADDRESS_IN,
  input  COUNTER_OUT,
  output [15:0] ALWAYS_OUT,
  output [15:0] ADDRESS_OUT
);

  wire not_1_out;

  not not_1 (not_1_out, COUNTER_OUT);
  Counter #(.max('hffff), .width(16)) counter_1 (
    .clr(RESET), .load(JUMP), .up(COUNTER_ENABLE), .count(COUNTER_ENABLE), .clk(CLOCK), .D(ADDRESS_IN),
    .Q(ALWAYS_OUT));  // open: carry
  assign ADDRESS_OUT = not_1_out ? ALWAYS_OUT : 16'bz;  // Controlled_Buffer controlled_buffer_1
endmodule

module memory_address_register (
  input  [3:0] DATA_IN,
  input  [3:0] MAR_WRITE,
  input  CLOCK,
  input  RESET,
  input  MAR_OUT,
  output [15:0] DATA_OUT
);

  wire [3:0] register_1_q, register_2_q, register_3_q, register_4_q;

  Register #(.width(4)) register_1 (.D(DATA_IN), .en(MAR_WRITE[0]), .clk(CLOCK), .Q(register_1_q), .clr(RESET));
  Register #(.width(4)) register_2 (.D(DATA_IN), .en(MAR_WRITE[1]), .clk(CLOCK), .Q(register_2_q), .clr(RESET));
  Register #(.width(4)) register_3 (.D(DATA_IN), .en(MAR_WRITE[2]), .clk(CLOCK), .Q(register_3_q), .clr(RESET));
  Register #(.width(4)) register_4 (.D(DATA_IN), .en(MAR_WRITE[3]), .clk(CLOCK), .Q(register_4_q), .clr(RESET));
  assign DATA_OUT[3:0] = MAR_OUT ? register_1_q : 4'bz;  // Controlled_Buffer controlled_buffer_1
  assign DATA_OUT[7:4] = MAR_OUT ? register_2_q : 4'bz;  // Controlled_Buffer controlled_buffer_2
  assign DATA_OUT[11:8] = MAR_OUT ? register_3_q : 4'bz;  // Controlled_Buffer controlled_buffer_3
  assign DATA_OUT[15:12] = MAR_OUT ? register_4_q : 4'bz;  // Controlled_Buffer controlled_buffer_4
endmodule

module alu (
  input  BORROW_IN,
  input  CARRY_IN,
  input  [3:0] A_IN,
  input  [3:0] B_IN,
  input  ENABLE,
  input  [1:0] SELECT_OP,
  output [3:0] DATA_OUT,
  output BORROW_OUT,
  output [3:0] FLAG_OUT
);

  wire [3:0] adder_1_out, subtractor_1_out;

  Adder #(.width(4)) adder_1 (.a(A_IN), .b(B_IN), .out(adder_1_out), .cin(CARRY_IN), .cout(FLAG_OUT[0]));
  Subtractor #(.width(4)) subtractor_1 (.a(A_IN), .b(B_IN), .out(subtractor_1_out), .bin(BORROW_IN), .bout(BORROW_OUT));
  Comparator #(.width(4)) comparator_1 (.a(A_IN), .b(B_IN), .gt(FLAG_OUT[1]), .eq(FLAG_OUT[2]), .lt(FLAG_OUT[3]));
  Multiplexer #(.enable("true"), .select(2), .width(4)) multiplexer_1 (
    .in1(adder_1_out), .in2(subtractor_1_out), .in3(FLAG_OUT), .out(DATA_OUT), .sel(SELECT_OP), .en(ENABLE));  // open: in0
endmodule

module register_file (
  input  [3:0] DATA_IN,
  input  [1:0] WRITE,
  input  WRITE_ENABLE,
  input  [1:0] SELECT_A,
  input  [1:0] SELECT_B,
  input  [3:0] FLAG_IN,
  input  FLAG_CHECK,
  input  CLOCK,
  input  RESET,
  output [3:0] DATA_OUT_A,
  output [3:0] DATA_OUT_B,
  output [3:0] FLAG_OUT
);

  wire and_1_out, decoder_1_out0, decoder_1_out1, decoder_1_out2, decoder_1_out3;
  wire [3:0] multiplexer_1_out, register_1_q, register_2_q, register_3_q;

  Decoder #(.select(2)) decoder_1 (
    .out0(decoder_1_out0), .out1(decoder_1_out1), .out2(decoder_1_out2), .out3(decoder_1_out3), .sel(WRITE),
    .en(WRITE_ENABLE));
  and and_1 (and_1_out, decoder_1_out3, FLAG_CHECK);
  Multiplexer #(.width(4)) multiplexer_1 (.in0(DATA_IN), .in1(FLAG_IN), .out(multiplexer_1_out), .sel(FLAG_CHECK));
  Register #(.width(4)) register_1 (.D(DATA_IN), .en(decoder_1_out0), .clk(CLOCK), .Q(register_1_q), .clr(RESET));
  Register #(.width(4)) register_2 (.D(DATA_IN), .en(decoder_1_out1), .clk(CLOCK), .Q(register_2_q), .clr(RESET));
  Register #(.width(4)) register_3 (.D(DATA_IN), .en(decoder_1_out2), .clk(CLOCK), .Q(register_3_q), .clr(RESET));
  Register #(.width(4)) register_4 (.D(multiplexer_1_out), .en(and_1_out), .clk(CLOCK), .Q(FLAG_OUT), .clr(RESET));
  Multiplexer #(.select(2), .width(4)) multiplexer_2 (
    .in0(register_1_q), .in1(register_2_q), .in2(register_3_q), .in3(FLAG_OUT), .out(DATA_OUT_A),
    .sel(SELECT_A));
  Multiplexer #(.select(2), .width(4)) multiplexer_3 (
    .in0(register_1_q), .in1(register_2_q), .in2(register_3_q), .in3(FLAG_OUT), .out(DATA_OUT_B),
    .sel(SELECT_B));

  // Notes on the sheet:
  //   FLAGS
endmodule

module register_memory_access (
  input  [3:0] DATA_IN,
  input  WRITE,
  input  CLOCK,
  input  RESET,
  output [3:0] DATA_OUT
);

  Register #(.width(4)) register_1 (.D(DATA_IN), .en(WRITE), .clk(CLOCK), .Q(DATA_OUT), .clr(RESET));
endmodule

module alu_memory_access (
  input  [3:0] DATA_IN,
  input  WRITE,
  input  CLOCK,
  input  RESET,
  output [3:0] DATA_OUT
);

  Register #(.width(4)) register_1 (.D(DATA_IN), .en(WRITE), .clk(CLOCK), .Q(DATA_OUT), .clr(RESET));
endmodule

module instruction_register (
  input  [3:0] DATA_IN,
  input  WRITE,
  input  CLOCK,
  input  RESET,
  input  READ,
  output [3:0] ALWAYS_OUT,
  output [3:0] DATA_OUT
);

  Register #(.width(4)) register_1 (.D(DATA_IN), .en(WRITE), .clk(CLOCK), .Q(ALWAYS_OUT), .clr(RESET));
  assign DATA_OUT = READ ? ALWAYS_OUT : 4'bz;  // Controlled_Buffer controlled_buffer_1
endmodule

module control_unit (
  input  [3:0] FLAG,
  input  [3:0] FROM_RAM,
  input  CLOCK,
  input  [3:0] FROM_INTRUCTION_REG,
  input  [3:0] FROM_STEP_COUNTER,
  output OUTPUT_HIGH_NIBLE_WRITE,
  output OUTPUT_LOW_NIBLE_WRITE,
  output READ_8_BIT_OUTPUT,
  output IO_selection_reg_write,
  output load_keyboard,
  output keyboard_read,
  output JUMP_EANBLE,
  output RAM_WRITE_FROM_DATA_BUS,
  output MAR_OUTPUT,
  output PC_OUT_DISABLE,
  output MAR_3_WRITE,
  output MAR_2_WRITE,
  output MAR_1_WRITE,
  output MAR_O_WRITE,
  output RMA_RESET,
  output AMA_REST,
  output READ_REG_FILE_TO_THE_BUS,
  output REGFILE_WRITE,
  output AMA_WRITE,
  output RMA_WRITE,
  output STEP_COUNTER_RESET,
  output READ_RAM,
  output INSTRUCTION_REG_WRITE,
  output COUNTER_ENABLE
);

  wire and_21_out, and_22_out, and_23_out, and_24_out, and_25_out, buffer_1_out, buffer_34_out,
       buffer_58_out, CONDITION_CHECK_STORE, controlled_buffer_2_out, controlled_buffer_3_out,
       controlled_buffer_4_out, decoder_1_out0, decoder_1_out1, decoder_1_out2, decoder_1_out3,
       decoder_1_out4, decoder_1_out5, decoder_1_out6, decoder_1_out7, decoder_1_out8, decoder_1_out9,
       decoder_1_out10, decoder_1_out11, decoder_1_out12, decoder_1_out13, decoder_2_out1, decoder_2_out2,
       decoder_2_out3, decoder_2_out4, decoder_2_out5, decoder_2_out6, decoder_2_out7, decoder_2_out8,
       decoder_2_out9, decoder_2_out10, decoder_3_out1, decoder_3_out2, decoder_3_out3, decoder_3_out4,
       decoder_3_out5, decoder_3_out6, decoder_4_out1, decoder_4_out2, decoder_4_out3, decoder_4_out4,
       decoder_4_out5, decoder_4_out6, decoder_4_out7, decoder_4_out8, decoder_4_out9, decoder_4_out10,
       decoder_4_out11, decoder_4_out12, decoder_4_out13, decoder_5_out1, decoder_5_out2, decoder_5_out3,
       decoder_5_out4, decoder_5_out5, decoder_5_out6, decoder_5_out7, decoder_5_out8, decoder_5_out9,
       decoder_5_out10, decoder_5_out11, decoder_5_out12, decoder_5_out13, decoder_6_out1, decoder_6_out2,
       decoder_6_out3, decoder_6_out4, decoder_6_out5, decoder_7_out1, decoder_7_out2, decoder_7_out3,
       decoder_7_out4, decoder_7_out5, decoder_7_out6, decoder_7_out7, decoder_8_out0, decoder_8_out1,
       decoder_8_out2, decoder_8_out3, decoder_9_out1, decoder_9_out2, decoder_9_out3, decoder_9_out4,
       decoder_9_out5, decoder_9_out6, decoder_9_out7, decoder_9_out8, decoder_9_out9, decoder_10_out1,
       decoder_10_out2, decoder_10_out3, decoder_10_out4, decoder_10_out5, decoder_10_out6, not_1_out,
       not_2_out, not_3_out, not_4_out, not_5_out, not_6_out, or_1_out;
  wire [3:0] and_17_out, register_1_q;
  wire [15:0] and_16_out;

  Register #(.width(4)) register_1 (
    .D(FROM_RAM), .en(CONDITION_CHECK_STORE), .clk(CLOCK), .Q(register_1_q), .clr(AMA_REST));
  not not_1 (not_1_out, FROM_INTRUCTION_REG[0]);
  not not_2 (not_2_out, FROM_INTRUCTION_REG[1]);
  not not_3 (not_3_out, FROM_INTRUCTION_REG[2]);
  not not_4 (not_4_out, FROM_INTRUCTION_REG[3]);
  LED led_1 (.in(and_16_out[15]));
  LED led_2 (.in(and_16_out[14]));
  LED led_3 (.in(and_16_out[13]));
  LED led_4 (.in(and_16_out[12]));
  LED led_5 (.in(and_16_out[11]));
  LED led_6 (.in(and_16_out[10]));
  and and_1 (and_16_out[15], FROM_INTRUCTION_REG[0], FROM_INTRUCTION_REG[1], FROM_INTRUCTION_REG[2], FROM_INTRUCTION_REG[3]);
  and and_2 (and_16_out[14], not_1_out, FROM_INTRUCTION_REG[1], FROM_INTRUCTION_REG[2], FROM_INTRUCTION_REG[3]);
  and and_3 (and_16_out[13], FROM_INTRUCTION_REG[0], not_2_out, FROM_INTRUCTION_REG[2], FROM_INTRUCTION_REG[3]);
  and and_4 (and_16_out[12], not_1_out, not_2_out, FROM_INTRUCTION_REG[2], FROM_INTRUCTION_REG[3]);
  and and_5 (and_16_out[11], FROM_INTRUCTION_REG[0], FROM_INTRUCTION_REG[1], not_3_out, FROM_INTRUCTION_REG[3]);
  and and_6 (and_16_out[10], not_1_out, FROM_INTRUCTION_REG[1], not_3_out, FROM_INTRUCTION_REG[3]);
  and and_7 (and_16_out[9], FROM_INTRUCTION_REG[0], not_2_out, not_3_out, FROM_INTRUCTION_REG[3]);
  and and_8 (and_16_out[8], not_1_out, not_2_out, not_3_out, FROM_INTRUCTION_REG[3]);
  and and_9 (and_16_out[7], FROM_INTRUCTION_REG[0], FROM_INTRUCTION_REG[1], FROM_INTRUCTION_REG[2], not_4_out);
  and and_10 (and_16_out[6], not_1_out, FROM_INTRUCTION_REG[1], FROM_INTRUCTION_REG[2], not_4_out);
  and and_11 (and_16_out[5], FROM_INTRUCTION_REG[0], not_2_out, FROM_INTRUCTION_REG[2], not_4_out);
  and and_12 (and_16_out[4], not_1_out, not_2_out, FROM_INTRUCTION_REG[2], not_4_out);
  and and_13 (and_16_out[3], FROM_INTRUCTION_REG[0], FROM_INTRUCTION_REG[1], not_3_out, not_4_out);
  and and_14 (and_16_out[2], not_1_out, FROM_INTRUCTION_REG[1], not_3_out, not_4_out);
  and and_15 (and_16_out[1], FROM_INTRUCTION_REG[0], not_2_out, not_3_out, not_4_out);
  and and_16 (and_16_out[0], not_1_out, not_2_out, not_3_out, not_4_out);
  LED led_7 (.in(and_16_out[9]));
  LED led_8 (.in(and_16_out[8]));
  LED led_9 (.in(and_16_out[7]));
  LED led_10 (.in(and_16_out[6]));
  LED led_11 (.in(and_16_out[5]));
  LED led_12 (.in(and_16_out[4]));
  LED led_13 (.in(and_16_out[3]));
  LED led_14 (.in(and_16_out[2]));
  not not_5 (not_5_out, FROM_STEP_COUNTER[0]);
  not not_6 (not_6_out, FROM_STEP_COUNTER[1]);
  LED led_15 (.in(and_16_out[1]));
  LED led_16 (.in(and_16_out[0]));
  and and_17 (and_17_out[0], FROM_STEP_COUNTER[1], FROM_STEP_COUNTER[0]);
  and and_18 (and_17_out[1], not_5_out, FROM_STEP_COUNTER[1]);
  and and_19 (and_17_out[2], FROM_STEP_COUNTER[0], not_6_out);
  and and_20 (and_17_out[3], not_5_out, not_6_out);
  LED led_17 (.in(and_17_out[0]));
  LED led_18 (.in(and_17_out[1]));
  LED led_19 (.in(and_17_out[2]));
  LED led_20 (.in(and_17_out[3]));
  Controlled_Buffer controlled_buffer_1 (.in(and_17_out[0]), .en(and_16_out[0]));  // open: out
  assign controlled_buffer_2_out = and_16_out[0] ? and_17_out[1] : 1'bz;  // Controlled_Buffer controlled_buffer_2
  assign controlled_buffer_3_out = and_16_out[0] ? and_17_out[2] : 1'bz;  // Controlled_Buffer controlled_buffer_3
  assign controlled_buffer_4_out = and_16_out[0] ? and_17_out[3] : 1'bz;  // Controlled_Buffer controlled_buffer_4
  Decoder #(.disabled("Z"), .select(4)) decoder_1 (
    .out0(decoder_1_out0), .out1(decoder_1_out1), .out2(decoder_1_out2), .out3(decoder_1_out3),
    .out4(decoder_1_out4), .out5(decoder_1_out5), .out6(decoder_1_out6), .out7(decoder_1_out7),
    .out8(decoder_1_out8), .out9(decoder_1_out9), .out10(decoder_1_out10), .out11(decoder_1_out11),
    .out12(decoder_1_out12), .out13(decoder_1_out13), .sel(FROM_STEP_COUNTER), .en(and_16_out[7]));  // open: out14, out15
  Decoder #(.disabled("Z"), .select(4)) decoder_2 (
    .out0(decoder_1_out0), .out1(decoder_2_out1), .out2(decoder_2_out2), .out3(decoder_2_out3),
    .out4(decoder_2_out4), .out5(decoder_2_out5), .out6(decoder_2_out6), .out7(decoder_2_out7),
    .out8(decoder_2_out8), .out9(decoder_2_out9), .out10(decoder_2_out10), .sel(FROM_STEP_COUNTER),
    .en(and_16_out[6]));  // open: out11, out12, out13, out14, out15
  Decoder #(.disabled("Z"), .select(3)) decoder_3 (
    .out0(decoder_1_out0), .out1(decoder_3_out1), .out2(decoder_3_out2), .out3(decoder_3_out3),
    .out4(decoder_3_out4), .out5(decoder_3_out5), .out6(decoder_3_out6), .sel(FROM_STEP_COUNTER[2:0]),
    .en(and_16_out[5]));  // open: out7
  Decoder #(.disabled("Z"), .select(4)) decoder_4 (
    .out0(decoder_1_out0), .out1(decoder_4_out1), .out2(decoder_4_out2), .out3(decoder_4_out3),
    .out4(decoder_4_out4), .out5(decoder_4_out5), .out6(decoder_4_out6), .out7(decoder_4_out7),
    .out8(decoder_4_out8), .out9(decoder_4_out9), .out10(decoder_4_out10), .out11(decoder_4_out11),
    .out12(decoder_4_out12), .out13(decoder_4_out13), .sel(FROM_STEP_COUNTER), .en(and_16_out[4]));  // open: out14, out15
  Decoder #(.disabled("Z"), .select(4)) decoder_5 (
    .out0(decoder_1_out0), .out1(decoder_5_out1), .out2(decoder_5_out2), .out3(decoder_5_out3),
    .out4(decoder_5_out4), .out5(decoder_5_out5), .out6(decoder_5_out6), .out7(decoder_5_out7),
    .out8(decoder_5_out8), .out9(decoder_5_out9), .out10(decoder_5_out10), .out11(decoder_5_out11),
    .out12(decoder_5_out12), .out13(decoder_5_out13), .sel(FROM_STEP_COUNTER), .en(and_16_out[3]));  // open: out14, out15
  Decoder #(.disabled("Z"), .select(3)) decoder_6 (
    .out0(decoder_1_out0), .out1(decoder_6_out1), .out2(decoder_6_out2), .out3(decoder_6_out3),
    .out4(decoder_6_out4), .out5(decoder_6_out5), .sel(FROM_STEP_COUNTER[2:0]), .en(and_16_out[2]));  // open: out6, out7
  Decoder #(.disabled("Z"), .select(3)) decoder_7 (
    .out0(decoder_1_out0), .out1(decoder_7_out1), .out2(decoder_7_out2), .out3(decoder_7_out3),
    .out4(decoder_7_out4), .out5(decoder_7_out5), .out6(decoder_7_out6), .out7(decoder_7_out7),
    .sel(FROM_STEP_COUNTER[2:0]), .en(and_16_out[1]));
  Decoder #(.disabled("Z"), .select(2)) decoder_8 (
    .out0(decoder_8_out0), .out1(decoder_8_out1), .out2(decoder_8_out2), .out3(decoder_8_out3),
    .sel(register_1_q[1:0]));  // open: en
  buf buffer_1 (buffer_1_out, decoder_1_out1);
  buf buffer_2 (buffer_1_out, decoder_1_out3);
  buf buffer_3 (decoder_5_out2, decoder_1_out4);
  buf buffer_4 (buffer_1_out, decoder_1_out5);
  buf buffer_5 (buffer_1_out, decoder_1_out7);
  buf buffer_6 (buffer_1_out, decoder_1_out9);
  buf buffer_7 (buffer_1_out, decoder_1_out11);
  buf buffer_8 (AMA_REST, decoder_1_out13);
  buf buffer_9 (buffer_1_out, decoder_2_out1);
  buf buffer_10 (decoder_5_out2, decoder_2_out2);
  buf buffer_11 (buffer_1_out, decoder_2_out3);
  buf buffer_12 (buffer_1_out, decoder_2_out5);
  buf buffer_13 (buffer_1_out, decoder_2_out7);
  buf buffer_14 (AMA_REST, decoder_2_out10);
  buf buffer_15 (buffer_1_out, decoder_3_out1);
  buf buffer_16 (buffer_1_out, decoder_3_out3);
  buf buffer_17 (buffer_1_out, decoder_3_out5);
  buf buffer_18 (AMA_REST, decoder_3_out6);
  buf buffer_19 (buffer_1_out, decoder_4_out1);
  buf buffer_20 (buffer_1_out, decoder_4_out3);
  buf buffer_21 (decoder_5_out2, decoder_4_out4);
  buf buffer_22 (buffer_1_out, decoder_4_out5);
  buf buffer_23 (buffer_1_out, decoder_4_out7);
  buf buffer_24 (buffer_1_out, decoder_4_out9);
  buf buffer_25 (buffer_1_out, decoder_4_out11);
  buf buffer_26 (decoder_5_out13, decoder_4_out13);
  buf buffer_27 (buffer_1_out, decoder_5_out1);
  buf buffer_28 (buffer_1_out, decoder_5_out3);
  buf buffer_29 (buffer_1_out, decoder_5_out5);
  buf buffer_30 (buffer_1_out, decoder_5_out7);
  buf buffer_31 (buffer_1_out, decoder_5_out9);
  buf buffer_32 (buffer_1_out, decoder_5_out11);
  buf buffer_33 (buffer_1_out, decoder_6_out1);
  buf buffer_34 (buffer_34_out, decoder_6_out2);
  buf buffer_35 (controlled_buffer_4_out, decoder_1_out0);
  buf buffer_36 (buffer_1_out, decoder_7_out1);
  buf buffer_37 (READ_RAM, decoder_1_out2);
  buf buffer_38 (CONDITION_CHECK_STORE, decoder_1_out2);
  buf buffer_39 (decoder_5_out4, decoder_1_out6);
  buf buffer_40 (decoder_5_out6, decoder_1_out8);
  buf buffer_41 (decoder_5_out4, decoder_2_out4);
  buf buffer_42 (decoder_5_out6, decoder_2_out6);
  buf buffer_43 (decoder_5_out8, decoder_2_out8);
  buf buffer_44 (decoder_5_out10, decoder_3_out2);
  buf buffer_45 (REGFILE_WRITE, decoder_3_out4);
  buf buffer_46 (READ_RAM, decoder_3_out4);
  buf buffer_47 (decoder_5_out4, decoder_4_out6);
  buf buffer_48 (decoder_5_out6, decoder_4_out8);
  buf buffer_49 (COUNTER_ENABLE, decoder_6_out3);
  buf buffer_50 (READ_REG_FILE_TO_THE_BUS, decoder_6_out4);
  buf buffer_51 (REGFILE_WRITE, decoder_6_out4);
  buf buffer_52 (AMA_REST, decoder_6_out5);
  buf buffer_53 (READ_RAM, decoder_7_out4);
  buf buffer_54 (REGFILE_WRITE, decoder_7_out5);
  buf buffer_55 (COUNTER_ENABLE, decoder_7_out6);
  and and_21 (and_21_out, FLAG[0], decoder_8_out0);
  and and_22 (and_22_out, FLAG[1], decoder_8_out1);
  and and_23 (and_23_out, FLAG[2], decoder_8_out2);
  and and_24 (and_24_out, FLAG[3], decoder_8_out3);
  buf buffer_56 (decoder_5_out8, decoder_1_out10);
  buf buffer_57 (MAR_OUTPUT, decoder_1_out12);
  buf buffer_58 (buffer_58_out, decoder_1_out12);
  buf buffer_59 (PC_OUT_DISABLE, decoder_1_out12);
  buf buffer_60 (JUMP_EANBLE, decoder_2_out9);
  buf buffer_61 (MAR_OUTPUT, decoder_2_out9);
  buf buffer_62 (PC_OUT_DISABLE, decoder_2_out9);
  buf buffer_63 (decoder_5_out10, decoder_4_out2);
  buf buffer_64 (decoder_5_out8, decoder_4_out10);
  buf buffer_65 (AMA_REST, decoder_5_out13);
  buf buffer_66 (COUNTER_ENABLE, decoder_7_out3);
  buf buffer_67 (AMA_REST, decoder_7_out7);
  // Buffer buffer_68 has open pins: in=decoder_7_out7, out=open
  buf buffer_69 (MAR_OUTPUT, decoder_4_out12);
  buf buffer_70 (PC_OUT_DISABLE, decoder_4_out12);
  buf buffer_71 (READ_REG_FILE_TO_THE_BUS, decoder_4_out12);
  buf buffer_72 (RAM_WRITE_FROM_DATA_BUS, decoder_4_out12);
  buf buffer_73 (REGFILE_WRITE, decoder_5_out12);
  buf buffer_74 (MAR_OUTPUT, decoder_5_out12);
  buf buffer_75 (PC_OUT_DISABLE, decoder_5_out12);
  buf buffer_76 (READ_RAM, decoder_5_out12);
  buf buffer_77 (MAR_3_WRITE, decoder_5_out2);
  buf buffer_78 (READ_RAM, decoder_5_out2);
  buf buffer_79 (READ_RAM, decoder_5_out4);
  buf buffer_80 (MAR_2_WRITE, decoder_5_out4);
  buf buffer_81 (READ_RAM, decoder_5_out6);
  buf buffer_82 (MAR_1_WRITE, decoder_5_out6);
  buf buffer_83 (READ_RAM, decoder_5_out8);
  buf buffer_84 (MAR_O_WRITE, decoder_5_out8);
  buf buffer_85 (READ_RAM, decoder_5_out10);
  buf buffer_86 (RMA_WRITE, decoder_5_out10);
  buf buffer_87 (RMA_WRITE, buffer_34_out);
  buf buffer_88 (READ_RAM, buffer_34_out);
  or or_1 (or_1_out, and_21_out, and_22_out, and_23_out, and_24_out);
  Pull_Resistor pull_resistor_1 (.node(buffer_58_out));
  buf buffer_89 (AMA_REST, controlled_buffer_2_out);
  buf buffer_90 (COUNTER_ENABLE, controlled_buffer_3_out);
  buf buffer_91 (READ_RAM, controlled_buffer_4_out);
  buf buffer_92 (INSTRUCTION_REG_WRITE, controlled_buffer_4_out);
  and and_25 (and_25_out, or_1_out, buffer_58_out);
  buf buffer_93 (JUMP_EANBLE, and_25_out);
  buf buffer_94 (AMA_WRITE, decoder_7_out4);
  Decoder #(.disabled("Z"), .select(4)) decoder_9 (
    .out0(decoder_1_out0), .out1(decoder_9_out1), .out2(decoder_9_out2), .out3(decoder_9_out3),
    .out4(decoder_9_out4), .out5(decoder_9_out5), .out6(decoder_9_out6), .out7(decoder_9_out7),
    .out8(decoder_9_out8), .out9(decoder_9_out9), .sel(FROM_STEP_COUNTER), .en(and_16_out[8]));  // open: out10, out11, out12, out13, out14, out15
  Decoder #(.disabled("Z"), .select(4)) decoder_10 (
    .out0(decoder_1_out0), .out1(decoder_10_out1), .out2(decoder_10_out2), .out3(decoder_10_out3),
    .out4(decoder_10_out4), .out5(decoder_10_out5), .out6(decoder_10_out6), .sel(FROM_STEP_COUNTER),
    .en(and_16_out[9]));  // open: out7, out8, out9, out10, out11, out12, out13, out14, out15
  buf buffer_95 (RMA_WRITE, decoder_7_out2);
  buf buffer_96 (READ_RAM, decoder_7_out2);
  buf buffer_97 (COUNTER_ENABLE, buffer_1_out);
  buf buffer_98 (READ_RAM, decoder_9_out2);
  buf buffer_99 (buffer_1_out, decoder_9_out1);
  buf buffer_100 (IO_selection_reg_write, decoder_9_out2);
  buf buffer_101 (buffer_1_out, decoder_9_out3);
  buf buffer_102 (READ_RAM, decoder_9_out4);
  buf buffer_103 (buffer_1_out, decoder_9_out5);
  buf buffer_104 (OUTPUT_HIGH_NIBLE_WRITE, decoder_9_out4);
  buf buffer_105 (buffer_1_out, decoder_9_out7);
  buf buffer_106 (READ_RAM, decoder_9_out6);
  buf buffer_107 (OUTPUT_LOW_NIBLE_WRITE, decoder_9_out6);
  buf buffer_108 (READ_8_BIT_OUTPUT, decoder_9_out8);
  buf buffer_109 (AMA_REST, decoder_9_out9);
  buf buffer_110 (buffer_1_out, decoder_10_out1);
  buf buffer_111 (buffer_1_out, decoder_10_out3);
  Pull_Resistor pull_resistor_2 (.node(JUMP_EANBLE));
  Pull_Resistor pull_resistor_3 (.node(RAM_WRITE_FROM_DATA_BUS));
  Pull_Resistor pull_resistor_4 (.node(MAR_OUTPUT));
  Pull_Resistor pull_resistor_5 (.node(REGFILE_WRITE));
  Pull_Resistor pull_resistor_6 (.node(CONDITION_CHECK_STORE));
  buf buffer_112 (READ_RAM, decoder_10_out2);
  buf buffer_113 (RMA_WRITE, decoder_10_out2);
  buf buffer_114 (keyboard_read, decoder_10_out4);
  buf buffer_115 (REGFILE_WRITE, decoder_10_out4);
  buf buffer_116 (load_keyboard, decoder_10_out5);
  buf buffer_117 (AMA_REST, decoder_10_out6);
  Pull_Resistor pull_resistor_7 (.node(PC_OUT_DISABLE));
  Pull_Resistor pull_resistor_8 (.node(MAR_3_WRITE));
  Pull_Resistor pull_resistor_9 (.node(MAR_2_WRITE));
  Pull_Resistor pull_resistor_10 (.node(MAR_1_WRITE));
  Pull_Resistor pull_resistor_11 (.node(MAR_O_WRITE));
  Pull_Resistor pull_resistor_12 (.node(AMA_WRITE));
  Pull_Resistor pull_resistor_13 (.node(RMA_WRITE));
  Pull_Resistor pull_resistor_14 (.node(AMA_REST));
  Pull_Resistor pull_resistor_15 (.node(READ_RAM));
  Pull_Resistor pull_resistor_16 (.node(INSTRUCTION_REG_WRITE));
  Pull_Resistor pull_resistor_17 (.node(READ_REG_FILE_TO_THE_BUS));
  Pull_Resistor pull_resistor_18 (.node(IO_selection_reg_write));
  Pull_Resistor pull_resistor_19 (.node(READ_8_BIT_OUTPUT));
  Pull_Resistor pull_resistor_20 (.node(OUTPUT_LOW_NIBLE_WRITE));
  Pull_Resistor pull_resistor_21 (.node(OUTPUT_HIGH_NIBLE_WRITE));
  Pull_Resistor pull_resistor_22 (.node(load_keyboard));
  Pull_Resistor pull_resistor_23 (.node(keyboard_read));

  assign RMA_RESET = AMA_REST;
  assign STEP_COUNTER_RESET = AMA_REST;

  // Other names for the same wires on the sheet: CONDITION_CHECK_RESET = AMA_REST

  // Notes on the sheet:
  //   buffer_1 drives only 1 and floats otherwise
  //   buffer_2 drives only 1 and floats otherwise
  //   buffer_3 drives only 1 and floats otherwise
  //   buffer_4 drives only 1 and floats otherwise
  //   buffer_5 drives only 1 and floats otherwise
  //   buffer_6 drives only 1 and floats otherwise
  //   buffer_7 drives only 1 and floats otherwise
  //   buffer_8 drives only 1 and floats otherwise
  //   buffer_9 drives only 1 and floats otherwise
  //   buffer_10 drives only 1 and floats otherwise
  //   buffer_11 drives only 1 and floats otherwise
  //   buffer_12 drives only 1 and floats otherwise
  //   buffer_13 drives only 1 and floats otherwise
  //   buffer_14 drives only 1 and floats otherwise
  //   buffer_15 drives only 1 and floats otherwise
  //   buffer_16 drives only 1 and floats otherwise
  //   buffer_17 drives only 1 and floats otherwise
  //   buffer_18 drives only 1 and floats otherwise
  //   buffer_19 drives only 1 and floats otherwise
  //   buffer_20 drives only 1 and floats otherwise
  //   buffer_21 drives only 1 and floats otherwise
  //   buffer_22 drives only 1 and floats otherwise
  //   buffer_23 drives only 1 and floats otherwise
  //   buffer_24 drives only 1 and floats otherwise
  //   buffer_25 drives only 1 and floats otherwise
  //   buffer_26 drives only 1 and floats otherwise
  //   buffer_27 drives only 1 and floats otherwise
  //   buffer_28 drives only 1 and floats otherwise
  //   buffer_29 drives only 1 and floats otherwise
  //   buffer_30 drives only 1 and floats otherwise
  //   buffer_31 drives only 1 and floats otherwise
  //   buffer_32 drives only 1 and floats otherwise
  //   buffer_33 drives only 1 and floats otherwise
  //   buffer_34 drives only 1 and floats otherwise
  //   buffer_35 drives only 1 and floats otherwise
  //   buffer_36 drives only 1 and floats otherwise
  //   buffer_37 drives only 1 and floats otherwise
  //   buffer_38 drives only 1 and floats otherwise
  //   buffer_39 drives only 1 and floats otherwise
  //   buffer_40 drives only 1 and floats otherwise
  //   buffer_41 drives only 1 and floats otherwise
  //   buffer_42 drives only 1 and floats otherwise
  //   buffer_43 drives only 1 and floats otherwise
  //   buffer_44 drives only 1 and floats otherwise
  //   buffer_45 drives only 1 and floats otherwise
  //   buffer_46 drives only 1 and floats otherwise
  //   buffer_47 drives only 1 and floats otherwise
  //   buffer_48 drives only 1 and floats otherwise
  //   buffer_49 drives only 1 and floats otherwise
  //   buffer_50 drives only 1 and floats otherwise
  //   buffer_51 drives only 1 and floats otherwise
  //   buffer_52 drives only 1 and floats otherwise
  //   buffer_53 drives only 1 and floats otherwise
  //   buffer_54 drives only 1 and floats otherwise
  //   buffer_55 drives only 1 and floats otherwise
  //   buffer_56 drives only 1 and floats otherwise
  //   buffer_57 drives only 1 and floats otherwise
  //   buffer_58 drives only 1 and floats otherwise
  //   buffer_59 drives only 1 and floats otherwise
  //   buffer_60 drives only 1 and floats otherwise
  //   buffer_61 drives only 1 and floats otherwise
  //   buffer_62 drives only 1 and floats otherwise
  //   buffer_63 drives only 1 and floats otherwise
  //   buffer_64 drives only 1 and floats otherwise
  //   buffer_65 drives only 1 and floats otherwise
  //   buffer_66 drives only 1 and floats otherwise
  //   buffer_67 drives only 1 and floats otherwise
  //   buffer_68 drives only 1 and floats otherwise
  //   buffer_69 drives only 1 and floats otherwise
  //   buffer_70 drives only 1 and floats otherwise
  //   buffer_71 drives only 1 and floats otherwise
  //   buffer_72 drives only 1 and floats otherwise
  //   buffer_73 drives only 1 and floats otherwise
  //   buffer_74 drives only 1 and floats otherwise
  //   buffer_75 drives only 1 and floats otherwise
  //   buffer_76 drives only 1 and floats otherwise
  //   buffer_77 drives only 1 and floats otherwise
  //   buffer_78 drives only 1 and floats otherwise
  //   buffer_79 drives only 1 and floats otherwise
  //   buffer_80 drives only 1 and floats otherwise
  //   buffer_81 drives only 1 and floats otherwise
  //   buffer_82 drives only 1 and floats otherwise
  //   buffer_83 drives only 1 and floats otherwise
  //   buffer_84 drives only 1 and floats otherwise
  //   buffer_85 drives only 1 and floats otherwise
  //   buffer_86 drives only 1 and floats otherwise
  //   buffer_87 drives only 1 and floats otherwise
  //   buffer_88 drives only 1 and floats otherwise
  //   buffer_89 drives only 1 and floats otherwise
  //   buffer_90 drives only 1 and floats otherwise
  //   buffer_91 drives only 1 and floats otherwise
  //   buffer_92 drives only 1 and floats otherwise
  //   buffer_93 drives only 1 and floats otherwise
  //   buffer_94 drives only 1 and floats otherwise
  //   buffer_95 drives only 1 and floats otherwise
  //   buffer_96 drives only 1 and floats otherwise
  //   buffer_97 drives only 1 and floats otherwise
  //   buffer_98 drives only 1 and floats otherwise
  //   buffer_99 drives only 1 and floats otherwise
  //   buffer_100 drives only 1 and floats otherwise
  //   buffer_101 drives only 1 and floats otherwise
  //   buffer_102 drives only 1 and floats otherwise
  //   buffer_103 drives only 1 and floats otherwise
  //   buffer_104 drives only 1 and floats otherwise
  //   buffer_105 drives only 1 and floats otherwise
  //   buffer_106 drives only 1 and floats otherwise
  //   buffer_107 drives only 1 and floats otherwise
  //   buffer_108 drives only 1 and floats otherwise
  //   buffer_109 drives only 1 and floats otherwise
  //   buffer_110 drives only 1 and floats otherwise
  //   buffer_111 drives only 1 and floats otherwise
  //   buffer_112 drives only 1 and floats otherwise
  //   buffer_113 drives only 1 and floats otherwise
  //   buffer_114 drives only 1 and floats otherwise
  //   buffer_115 drives only 1 and floats otherwise
  //   buffer_116 drives only 1 and floats otherwise
  //   buffer_117 drives only 1 and floats otherwise
endmodule

module step_counter (
  input  RESET,
  input  CLOCK,
  output [3:0] DATA_OUT
);

  Counter #(.max('hf), .width(4)) counter_1 (
    .clr(RESET), .up(1'b1), .count(1'b1), .clk(CLOCK), .Q(DATA_OUT));  // open: load, D, carry
endmodule

module io_selection_register (
  input  [3:0] DATA_IN,
  input  WRITE,
  input  READ,
  input  CLOCK,
  input  RESET,
  output [3:0] ALWAYS_OUT,
  output [3:0] DATA_OUT
);

  Register #(.width(4)) register_1 (.D(DATA_IN), .en(WRITE), .clk(CLOCK), .Q(ALWAYS_OUT), .clr(RESET));
  assign DATA_OUT = READ ? ALWAYS_OUT : 4'bz;  // Controlled_Buffer controlled_buffer_1
endmodule

module io_register (
  input  [3:0] DATA_IN,
  input  WRITE_LOW,
  input  WRITE_HIGH,
  input  READ,
  input  CLOCK,
  input  RESET,
  output [7:0] ALWAYS_OUT,
  output [7:0] DATA_OUT
);

  Register #(.width(4)) register_1 (.D(DATA_IN), .en(WRITE_LOW), .clk(CLOCK), .Q(ALWAYS_OUT[3:0]), .clr(RESET));
  Register #(.width(4)) register_2 (.D(DATA_IN), .en(WRITE_HIGH), .clk(CLOCK), .Q(ALWAYS_OUT[7:4]), .clr(RESET));
  assign DATA_OUT = READ ? ALWAYS_OUT : 8'bz;  // Controlled_Buffer controlled_buffer_1
endmodule

module control_unit_2 (
  input  [3:0] FLAG,
  input  [3:0] FROM_RAM,
  input  CLOCK,
  input  [3:0] STEP,
  input  [3:0] INSTRUCTION,
  output JUMP_ENABLE,
  output RAM_READ,
  output REGFILE_READ,
  output MAR_READ,
  output IO_READ,
  output KEYBOARD_READ,
  output INSTRUSTION_REG_WRITE,
  output RMA_WRITE,
  output AMA_WRITE,
  output REGFILE_WRITE,
  output MAR_3,
  output RAM_WRITE,
  output MAR_2,
  output MAR_1,
  output IO_WRITE,
  output MAR_0,
  output KEYBOARD_WRITE,
  output NIBLE_HIGH_WRITE,
  output NIBLE_LOW_WRITE,
  output PC_ENABLE,
  output PC_OUT_DISABLE,
  output RMA_RESET,
  output AMA_RESET,
  output STEP_COUNTER_RESET
);

  wire and_1_out, and_2_out, and_3_out, and_4_out, and_5_out, and_6_out, and_7_out, and_8_out, and_9_out,
       CONDITION_CHECK_STORE, decoder_1_out0, decoder_1_out1, decoder_1_out2, decoder_1_out3,
       micro_cycle_1_jump_enable, not_1_out, not_2_out, not_3_out, not_4_out, not_5_out, or_1_out;
  wire [3:0] register_1_q;

  Register #(.width(4)) register_1 (
    .D(FROM_RAM), .en(CONDITION_CHECK_STORE), .clk(CLOCK), .Q(register_1_q), .clr(AMA_RESET));
  micro_cycle micro_cycle_1 (
    .INSTRUCTION(INSTRUCTION), .STEP(STEP), .RAM_READ(RAM_READ), .REGFILE_READ(REGFILE_READ),
    .MAR_READ(MAR_READ), .IO_READ(IO_READ), .KEYBOARD_READ(KEYBOARD_READ),
    .INSTRUCTION_REG_WRITE(INSTRUSTION_REG_WRITE), .RMA_WRITE(RMA_WRITE), .AMA_WRITE(AMA_WRITE),
    .REGFILE_WRITE(REGFILE_WRITE), .RAM_WRITE(RAM_WRITE), .MAR_WRITE({MAR_3, MAR_2, MAR_1, MAR_0}),
    .IO_WRITE(IO_WRITE), .KEYBOARD_WRITE(KEYBOARD_WRITE), .NIBLE_HIGH_WRITE(NIBLE_HIGH_WRITE),
    .NIBLE_LOW_WRITE(NIBLE_LOW_WRITE), .PC_ENABLE(PC_ENABLE), .PC_OUT_DISABLE(PC_OUT_DISABLE),
    .JUMP_ENABLE(micro_cycle_1_jump_enable), .RMA_RESET(AMA_RESET), .AMA_RESET(AMA_RESET),
    .STEP_RESET(STEP_COUNTER_RESET));
  Decoder #(.disabled("Z"), .select(2)) decoder_1 (
    .out0(decoder_1_out0), .out1(decoder_1_out1), .out2(decoder_1_out2), .out3(decoder_1_out3),
    .sel(register_1_q[1:0]));  // open: en
  not not_1 (not_1_out, INSTRUCTION[3]);
  and and_1 (and_1_out, not_1_out, INSTRUCTION[2], INSTRUCTION[1], INSTRUCTION[0]);
  not not_2 (not_2_out, STEP[0]);
  not not_3 (not_3_out, STEP[2]);
  not not_4 (not_4_out, STEP[3]);
  not not_5 (not_5_out, INSTRUCTION[3]);
  and and_2 (and_2_out, FLAG[0], decoder_1_out0);
  and and_3 (and_3_out, FLAG[1], decoder_1_out1);
  and and_4 (and_4_out, FLAG[2], decoder_1_out2);
  and and_5 (and_5_out, FLAG[3], decoder_1_out3);
  and and_6 (and_6_out, not_2_out, STEP[1], not_3_out, not_4_out);
  and and_7 (and_7_out, not_5_out, INSTRUCTION[2], INSTRUCTION[1], INSTRUCTION[0]);
  and and_8 (and_8_out, and_6_out, and_7_out);
  or or_1 (or_1_out, and_2_out, and_3_out, and_4_out, and_5_out);
  buf or_2 (CONDITION_CHECK_STORE, and_8_out);  // OR_Gate
  and and_9 (and_9_out, or_1_out, micro_cycle_1_jump_enable);
  Multiplexer multiplexer_1 (.in0(micro_cycle_1_jump_enable), .in1(and_9_out), .out(JUMP_ENABLE), .sel(and_1_out));

  assign RMA_RESET = AMA_RESET;

  // Other names for the same wires on the sheet: CONDITION_CHECK_RESET = AMA_RESET
endmodule

module micro_cycles (
  input  [3:0] INSTRUCTION,
  input  [3:0] STEP,
  output RAM_READ,
  output REGFILE_READ,
  output MAR_READ,
  output IO_READ,
  output KEYBOARD_READ,
  output INSTRUCTION_REG_WRITE,
  output RMA_WRITE,
  output AMA_WRITE,
  output REGFILE_WRITE,
  output RAM_WRITE,
  output [3:0] MAR_WRITE,
  output IO_WRITE,
  output KEYBOARD_WRITE,
  output NIBLE_HIGH_WRITE,
  output NIBLE_LOW_WRITE,
  output PC_ENABLE,
  output PC_OUT_DISABLE,
  output JUMP_ENABLE,
  output RMA_RESET,
  output AMA_RESET,
  output STEP_COUNTER_RESET
);

  wire and_1_out, and_2_out, and_3_out, and_4_out, and_5_out, and_6_out, and_7_out, and_8_out, and_9_out,
       and_10_out, and_11_out, and_12_out, and_13_out, and_14_out, and_15_out, and_16_out, and_17_out,
       and_18_out, and_19_out, and_20_out, and_21_out, and_22_out, and_25_out, and_26_out, not_1_out,
       not_2_out, not_3_out, not_4_out, not_5_out, not_6_out, not_7_out, not_8_out;

  not not_1 (not_1_out, INSTRUCTION[3]);
  not not_2 (not_2_out, INSTRUCTION[2]);
  not not_3 (not_3_out, INSTRUCTION[1]);
  not not_4 (not_4_out, INSTRUCTION[0]);
  not not_5 (not_5_out, STEP[3]);
  not not_6 (not_6_out, STEP[2]);
  not not_7 (not_7_out, STEP[1]);
  not not_8 (not_8_out, STEP[0]);
  and and_1 (and_1_out, INSTRUCTION[3], INSTRUCTION[2], not_3_out, not_4_out, not_5_out, not_6_out, STEP[1], STEP[0]);
  and and_2 (and_2_out, not_1_out, INSTRUCTION[2], not_4_out, not_5_out, not_8_out);
  and and_3 (and_3_out, INSTRUCTION[3], not_2_out, not_3_out, not_4_out, not_5_out, not_8_out);
  and and_4 (and_4_out, not_1_out, INSTRUCTION[2], not_3_out, not_4_out, not_6_out, not_8_out);
  and and_5 (and_5_out, not_1_out, INSTRUCTION[0], not_5_out, not_7_out, not_8_out);
  and and_6 (and_6_out, not_1_out, INSTRUCTION[1], not_5_out, not_6_out, not_8_out);
  and and_7 (and_7_out, INSTRUCTION[3], not_2_out, INSTRUCTION[1], not_4_out, not_5_out, STEP[1], STEP[0]);
  and and_8 (and_8_out, INSTRUCTION[3], not_2_out, not_4_out, not_5_out, STEP[2], not_7_out, not_8_out);
  and and_9 (and_9_out, not_1_out, INSTRUCTION[1], INSTRUCTION[0], not_5_out, not_8_out);
  and and_10 (and_10_out, not_1_out, INSTRUCTION[1], INSTRUCTION[0], not_6_out, not_8_out);
  and and_11 (and_11_out, not_1_out, not_2_out, INSTRUCTION[1], INSTRUCTION[0], not_7_out, not_8_out);
  and and_12 (and_12_out, not_2_out, not_3_out, not_5_out, not_6_out, not_7_out, not_8_out);
  and and_13 (and_13_out, not_1_out, INSTRUCTION[0], not_5_out, not_6_out, not_8_out);
  and and_14 (and_14_out, not_2_out, not_3_out, INSTRUCTION[0], not_5_out, not_6_out, not_8_out);
  and and_15 (and_15_out, not_1_out, INSTRUCTION[2], not_4_out, not_6_out, not_7_out, not_8_out);
  and and_16 (and_16_out, INSTRUCTION[3], INSTRUCTION[2], not_3_out, not_4_out, not_5_out, STEP[2], not_7_out, not_8_out);
  and and_17 (and_17_out, not_1_out, INSTRUCTION[2], not_3_out, not_4_out, STEP[3], STEP[2], not_7_out, not_8_out);
  and and_18 (and_18_out, INSTRUCTION[3], INSTRUCTION[2], not_3_out, not_4_out, not_5_out, STEP[1], STEP[0]);
  and and_19 (and_19_out, INSTRUCTION[3], INSTRUCTION[2], not_3_out, not_4_out, not_5_out, STEP[2], not_7_out, not_8_out);
  and and_20 (and_20_out, not_1_out, INSTRUCTION[2], INSTRUCTION[1], not_4_out, STEP[3], not_6_out, not_7_out, STEP[0]);
  and and_21 (and_21_out, not_1_out, INSTRUCTION[1], INSTRUCTION[0], STEP[3], STEP[2], not_7_out, not_8_out);
  and and_22 (and_22_out, not_1_out, INSTRUCTION[2], not_3_out, not_4_out, STEP[3], STEP[2], not_7_out, not_8_out);
  and and_23 (IO_READ, STEP[3], not_6_out, not_7_out, not_8_out, INSTRUCTION[3], not_2_out, not_3_out, not_4_out);
  and and_24 (KEYBOARD_READ, INSTRUCTION[3], not_2_out, not_3_out, INSTRUCTION[0], not_5_out, STEP[2], not_7_out, not_8_out);
  and and_25 (and_25_out, not_1_out, not_5_out, not_6_out, not_7_out, not_8_out);
  and and_26 (and_26_out, not_2_out, not_3_out, not_5_out, not_6_out, not_7_out, not_8_out);
  or or_1 (REGFILE_READ, and_16_out, and_17_out);
  or or_2 (MAR_READ, and_18_out, and_19_out, and_20_out, and_21_out, and_22_out);
  or or_3 (INSTRUCTION_REG_WRITE, and_25_out, and_26_out);
  or or_4 (RAM_READ, and_1_out, and_2_out, and_3_out, and_4_out, and_5_out, and_6_out, and_7_out, and_8_out, and_9_out, and_10_out, and_11_out, and_12_out, and_13_out, and_14_out, and_15_out);

  assign AMA_RESET = 1'b0;
  assign AMA_WRITE = 1'b0;
  assign IO_WRITE = 1'b0;
  assign JUMP_ENABLE = 1'b0;
  assign KEYBOARD_WRITE = 1'b0;
  assign MAR_WRITE = 4'b0000;
  assign NIBLE_HIGH_WRITE = 1'b0;
  assign NIBLE_LOW_WRITE = 1'b0;
  assign PC_ENABLE = 1'b0;
  assign PC_OUT_DISABLE = 1'b0;
  assign RAM_WRITE = 1'b0;
  assign REGFILE_WRITE = 1'b0;
  assign RMA_RESET = 1'b0;
  assign RMA_WRITE = 1'b0;
  assign STEP_COUNTER_RESET = 1'b0;
endmodule

module micro_cycle (
  input  [3:0] INSTRUCTION,
  input  [3:0] STEP,
  output RAM_READ,
  output REGFILE_READ,
  output MAR_READ,
  output IO_READ,
  output KEYBOARD_READ,
  output INSTRUCTION_REG_WRITE,
  output RMA_WRITE,
  output AMA_WRITE,
  output REGFILE_WRITE,
  output RAM_WRITE,
  output [3:0] MAR_WRITE,
  output IO_WRITE,
  output KEYBOARD_WRITE,
  output NIBLE_HIGH_WRITE,
  output NIBLE_LOW_WRITE,
  output PC_ENABLE,
  output PC_OUT_DISABLE,
  output JUMP_ENABLE,
  output RMA_RESET,
  output AMA_RESET,
  output STEP_RESET
);

  wire and_1_out, and_2_out, and_3_out, and_4_out, and_5_out, and_6_out, and_7_out, and_8_out, and_9_out,
       and_10_out, and_11_out, and_12_out, and_13_out, and_14_out, and_15_out, and_16_out, and_20_out,
       and_21_out, and_22_out, and_23_out, and_25_out, and_26_out, and_27_out, and_28_out, and_29_out,
       and_31_out, and_32_out, and_33_out, and_34_out, and_35_out, and_36_out, and_37_out, and_38_out,
       and_39_out, and_40_out, and_41_out, and_42_out, and_43_out, and_44_out, and_45_out, and_46_out,
       and_51_out, and_52_out, and_53_out, and_54_out, and_55_out, and_56_out, and_57_out, and_58_out,
       and_59_out, and_60_out, and_61_out, and_62_out, and_63_out, and_64_out, and_65_out, and_66_out,
       and_67_out, and_68_out, and_69_out, and_70_out, and_71_out, and_72_out, and_73_out, and_74_out,
       and_75_out, and_76_out, and_77_out, and_78_out, and_79_out, and_80_out, and_81_out, and_82_out,
       and_83_out, and_84_out, and_85_out, and_86_out, and_87_out, and_88_out, and_89_out, and_90_out,
       not_1_out, not_2_out, not_3_out, not_4_out, not_5_out, not_6_out, not_7_out, not_8_out;

  not not_1 (not_1_out, INSTRUCTION[3]);
  not not_2 (not_2_out, INSTRUCTION[2]);
  not not_3 (not_3_out, INSTRUCTION[1]);
  not not_4 (not_4_out, INSTRUCTION[0]);
  not not_5 (not_5_out, STEP[3]);
  not not_6 (not_6_out, STEP[2]);
  not not_7 (not_7_out, STEP[1]);
  not not_8 (not_8_out, STEP[0]);
  and and_1 (and_1_out, not_5_out, not_6_out, not_7_out, not_8_out);
  and and_2 (and_2_out, INSTRUCTION[3], not_4_out, not_5_out, not_8_out);
  and and_3 (and_3_out, INSTRUCTION[2], not_4_out, not_5_out, not_8_out);
  and and_4 (and_4_out, INSTRUCTION[2], not_3_out, not_4_out, not_6_out, not_8_out);
  and and_5 (and_5_out, INSTRUCTION[0], not_5_out, not_6_out, not_8_out);
  and and_6 (and_6_out, not_1_out, INSTRUCTION[0], not_5_out, not_7_out, not_8_out);
  and and_7 (and_7_out, INSTRUCTION[1], not_5_out, not_6_out, not_8_out);
  and and_8 (and_8_out, INSTRUCTION[1], INSTRUCTION[0], not_5_out, not_8_out);
  and and_9 (and_9_out, INSTRUCTION[1], INSTRUCTION[0], not_6_out, not_8_out);
  and and_10 (and_10_out, not_2_out, INSTRUCTION[1], INSTRUCTION[0], not_7_out, not_8_out);
  and and_11 (and_11_out, INSTRUCTION[2], not_4_out, not_6_out, not_7_out, not_8_out);
  and and_12 (and_12_out, not_1_out, not_2_out, INSTRUCTION[1], not_4_out, not_5_out, STEP[2], not_7_out, not_8_out);
  and and_13 (and_13_out, not_1_out, INSTRUCTION[2], not_3_out, not_4_out, STEP[3], STEP[2], not_7_out, not_8_out);
  and and_14 (and_14_out, INSTRUCTION[2], INSTRUCTION[1], not_4_out, STEP[3], not_6_out, not_7_out, STEP[0]);
  and and_15 (and_15_out, INSTRUCTION[1], INSTRUCTION[0], STEP[3], STEP[2], not_7_out, not_8_out);
  and and_16 (and_16_out, INSTRUCTION[2], not_3_out, not_4_out, STEP[3], STEP[2], not_7_out, not_8_out);
  and and_17 (IO_READ, INSTRUCTION[3], not_4_out, STEP[3], not_6_out, not_7_out, not_8_out);
  and and_18 (KEYBOARD_READ, INSTRUCTION[3], INSTRUCTION[0], not_5_out, STEP[2], not_7_out, not_8_out);
  and and_19 (INSTRUCTION_REG_WRITE, not_5_out, not_6_out, not_7_out, not_8_out);
  and and_20 (and_20_out, not_3_out, INSTRUCTION[0], not_5_out, not_6_out, STEP[1], not_8_out);
  and and_21 (and_21_out, not_2_out, INSTRUCTION[1], not_4_out, not_5_out, not_6_out, STEP[1], not_8_out);
  and and_22 (and_22_out, INSTRUCTION[2], not_3_out, not_5_out, not_6_out, STEP[1], not_8_out);
  and and_23 (and_23_out, not_2_out, INSTRUCTION[1], INSTRUCTION[0], STEP[3], not_6_out, STEP[1], not_8_out);
  and and_24 (AMA_WRITE, not_1_out, not_2_out, not_3_out, INSTRUCTION[0], not_5_out, STEP[2], not_7_out, not_8_out);
  and and_25 (and_25_out, not_2_out, INSTRUCTION[1], not_4_out, not_5_out, STEP[2], not_7_out, not_8_out);
  and and_26 (and_26_out, INSTRUCTION[2], not_3_out, INSTRUCTION[0], not_5_out, STEP[2], not_7_out, not_8_out);
  and and_27 (and_27_out, INSTRUCTION[3], INSTRUCTION[0], not_5_out, STEP[2], not_7_out, not_8_out);
  and and_28 (and_28_out, not_1_out, not_2_out, not_3_out, INSTRUCTION[0], not_5_out, STEP[2], not_7_out, STEP[0]);
  and and_29 (and_29_out, not_2_out, INSTRUCTION[1], INSTRUCTION[0], STEP[3], STEP[2], not_7_out, not_8_out);
  and and_30 (RAM_WRITE, INSTRUCTION[2], not_3_out, not_4_out, STEP[3], STEP[2], not_7_out, not_8_out);
  and and_31 (and_31_out, not_2_out, INSTRUCTION[1], INSTRUCTION[0], not_5_out, not_6_out, STEP[1], not_8_out);
  and and_32 (and_32_out, INSTRUCTION[2], INSTRUCTION[1], not_4_out, not_5_out, not_6_out, STEP[1], not_8_out);
  and and_33 (and_33_out, INSTRUCTION[2], not_3_out, not_4_out, not_5_out, STEP[2], not_7_out, not_8_out);
  and and_34 (and_34_out, INSTRUCTION[2], INSTRUCTION[1], INSTRUCTION[0], not_5_out, STEP[2], not_7_out, not_8_out);
  and and_35 (and_35_out, not_2_out, INSTRUCTION[1], INSTRUCTION[0], not_5_out, STEP[2], not_7_out, not_8_out);
  and and_36 (and_36_out, INSTRUCTION[2], INSTRUCTION[1], not_4_out, not_5_out, STEP[2], not_7_out, not_8_out);
  and and_37 (and_37_out, INSTRUCTION[2], not_3_out, not_4_out, not_5_out, STEP[2], STEP[1], not_8_out);
  and and_38 (and_38_out, INSTRUCTION[2], INSTRUCTION[1], INSTRUCTION[0], not_5_out, STEP[2], STEP[1], not_8_out);
  and and_39 (and_39_out, not_2_out, INSTRUCTION[1], INSTRUCTION[0], not_5_out, STEP[2], STEP[1], not_8_out);
  and and_40 (and_40_out, INSTRUCTION[2], INSTRUCTION[1], not_4_out, not_5_out, STEP[2], STEP[1], not_8_out);
  and and_41 (and_41_out, INSTRUCTION[2], not_3_out, not_4_out, STEP[3], not_6_out, not_7_out, not_8_out);
  and and_42 (and_42_out, INSTRUCTION[2], INSTRUCTION[1], INSTRUCTION[0], STEP[3], not_6_out, not_7_out, not_8_out);
  and and_43 (and_43_out, not_2_out, INSTRUCTION[1], INSTRUCTION[0], STEP[3], not_6_out, not_7_out, not_8_out);
  and and_44 (and_44_out, INSTRUCTION[2], INSTRUCTION[1], not_4_out, STEP[3], not_6_out, not_7_out, not_8_out);
  and and_45 (and_45_out, INSTRUCTION[2], not_3_out, not_4_out, STEP[3], not_6_out, STEP[1], not_8_out);
  and and_46 (and_46_out, INSTRUCTION[2], INSTRUCTION[1], INSTRUCTION[0], STEP[3], not_6_out, STEP[1], not_8_out);
  and and_47 (IO_WRITE, INSTRUCTION[3], not_4_out, not_5_out, not_6_out, STEP[1], not_8_out);
  and and_48 (KEYBOARD_WRITE, INSTRUCTION[3], INSTRUCTION[0], not_5_out, STEP[2], not_7_out, STEP[0]);
  and and_49 (NIBLE_HIGH_WRITE, INSTRUCTION[3], not_4_out, not_5_out, STEP[2], not_7_out, not_8_out);
  and and_50 (NIBLE_LOW_WRITE, INSTRUCTION[3], not_4_out, not_5_out, STEP[2], STEP[1], not_8_out);
  and and_51 (and_51_out, not_5_out, not_6_out, not_7_out, STEP[0]);
  and and_52 (and_52_out, INSTRUCTION[3], not_4_out, not_5_out, STEP[0]);
  and and_53 (and_53_out, INSTRUCTION[2], not_4_out, not_5_out, STEP[0]);
  and and_54 (and_54_out, INSTRUCTION[2], not_3_out, not_4_out, not_6_out, STEP[0]);
  and and_55 (and_55_out, INSTRUCTION[0], not_5_out, not_6_out, STEP[0]);
  and and_56 (and_56_out, INSTRUCTION[2], not_5_out, not_7_out, STEP[0]);
  and and_57 (and_57_out, not_1_out, not_2_out, not_3_out, INSTRUCTION[0], not_5_out, STEP[2], STEP[1], not_8_out);
  and and_58 (and_58_out, INSTRUCTION[1], not_5_out, not_6_out, STEP[0]);
  and and_59 (and_59_out, INSTRUCTION[1], INSTRUCTION[0], not_5_out, STEP[0]);
  and and_60 (and_60_out, INSTRUCTION[1], INSTRUCTION[0], not_6_out, STEP[0]);
  and and_61 (and_61_out, INSTRUCTION[2], INSTRUCTION[1], not_4_out, STEP[3], not_6_out, not_7_out, STEP[0]);
  and and_62 (and_62_out, INSTRUCTION[1], INSTRUCTION[0], STEP[3], STEP[2], not_7_out, not_8_out);
  and and_63 (and_63_out, INSTRUCTION[2], not_3_out, not_4_out, STEP[3], STEP[2], not_7_out, not_8_out);
  and and_64 (and_64_out, INSTRUCTION[2], INSTRUCTION[1], not_4_out, STEP[3], not_6_out, not_7_out, STEP[0]);
  and and_65 (and_65_out, INSTRUCTION[2], INSTRUCTION[1], INSTRUCTION[0], STEP[3], STEP[2], not_7_out, not_8_out);
  and and_66 (and_66_out, not_1_out, not_2_out, INSTRUCTION[1], not_4_out, not_5_out, STEP[2], not_7_out, STEP[0]);
  and and_67 (and_67_out, INSTRUCTION[3], not_4_out, STEP[3], not_6_out, not_7_out, STEP[0]);
  and and_68 (and_68_out, INSTRUCTION[2], INSTRUCTION[1], not_4_out, STEP[3], not_6_out, STEP[1], not_8_out);
  and and_69 (and_69_out, INSTRUCTION[2], not_3_out, not_4_out, STEP[3], STEP[2], not_7_out, STEP[0]);
  and and_70 (and_70_out, INSTRUCTION[2], not_3_out, INSTRUCTION[0], not_5_out, STEP[2], STEP[1], not_8_out);
  and and_71 (and_71_out, INSTRUCTION[3], INSTRUCTION[0], not_5_out, STEP[2], STEP[1], not_8_out);
  and and_72 (and_72_out, not_1_out, not_2_out, not_3_out, INSTRUCTION[0], not_5_out, STEP[2], STEP[1], STEP[0]);
  and and_73 (and_73_out, INSTRUCTION[1], INSTRUCTION[0], STEP[3], STEP[2], not_7_out, STEP[0]);
  and and_74 (and_74_out, not_1_out, not_2_out, INSTRUCTION[1], not_4_out, not_5_out, STEP[2], not_7_out, STEP[0]);
  and and_75 (and_75_out, INSTRUCTION[3], not_4_out, STEP[3], not_6_out, not_7_out, STEP[0]);
  and and_76 (and_76_out, INSTRUCTION[2], INSTRUCTION[1], not_4_out, STEP[3], not_6_out, STEP[1], not_8_out);
  and and_77 (and_77_out, INSTRUCTION[2], not_3_out, not_4_out, STEP[3], STEP[2], not_7_out, STEP[0]);
  and and_78 (and_78_out, INSTRUCTION[2], not_3_out, INSTRUCTION[0], not_5_out, STEP[2], STEP[1], not_8_out);
  and and_79 (and_79_out, INSTRUCTION[3], INSTRUCTION[0], not_5_out, STEP[2], STEP[1], not_8_out);
  and and_80 (and_80_out, not_1_out, not_2_out, not_3_out, INSTRUCTION[0], not_5_out, STEP[2], STEP[1], STEP[0]);
  and and_81 (and_81_out, INSTRUCTION[1], INSTRUCTION[0], STEP[3], STEP[2], not_7_out, STEP[0]);
  and and_82 (and_82_out, not_1_out, not_2_out, not_3_out, not_4_out, not_5_out, not_6_out, STEP[1], not_8_out);
  and and_83 (and_83_out, not_2_out, INSTRUCTION[1], not_4_out, not_5_out, STEP[2], not_7_out, STEP[0]);
  and and_84 (and_84_out, INSTRUCTION[2], not_3_out, INSTRUCTION[0], not_5_out, STEP[2], STEP[1], not_8_out);
  and and_85 (and_85_out, INSTRUCTION[3], INSTRUCTION[0], not_5_out, STEP[2], STEP[1], not_8_out);
  and and_86 (and_86_out, not_1_out, not_2_out, not_3_out, INSTRUCTION[0], not_5_out, STEP[2], STEP[1], STEP[0]);
  and and_87 (and_87_out, INSTRUCTION[3], not_4_out, STEP[3], not_6_out, not_7_out, STEP[0]);
  and and_88 (and_88_out, INSTRUCTION[2], INSTRUCTION[1], not_4_out, STEP[3], not_6_out, STEP[1], not_8_out);
  and and_89 (and_89_out, INSTRUCTION[1], INSTRUCTION[0], STEP[3], STEP[2], not_7_out, STEP[0]);
  and and_90 (and_90_out, INSTRUCTION[2], not_3_out, not_4_out, STEP[3], STEP[2], not_7_out, STEP[0]);
  or or_1 (RAM_READ, and_1_out, and_2_out, and_3_out, and_4_out, and_5_out, and_6_out, and_7_out, and_8_out, and_9_out, and_10_out, and_11_out);
  or or_2 (REGFILE_READ, and_12_out, and_13_out);
  or or_3 (MAR_READ, and_14_out, and_15_out, and_16_out);
  or or_4 (RMA_WRITE, and_20_out, and_21_out, and_22_out, and_23_out);
  or or_5 (REGFILE_WRITE, and_25_out, and_26_out, and_27_out, and_28_out, and_29_out);
  or or_6 (MAR_WRITE[3], and_31_out, and_32_out, and_33_out, and_34_out);
  or or_7 (MAR_WRITE[2], and_35_out, and_36_out, and_37_out, and_38_out);
  or or_8 (MAR_WRITE[1], and_39_out, and_40_out, and_41_out, and_42_out);
  or or_9 (MAR_WRITE[0], and_43_out, and_44_out, and_45_out, and_46_out);
  or or_10 (PC_ENABLE, and_51_out, and_52_out, and_53_out, and_54_out, and_55_out, and_56_out, and_57_out, and_58_out, and_59_out, and_60_out);
  or or_11 (PC_OUT_DISABLE, and_61_out, and_62_out, and_63_out);
  or or_12 (JUMP_ENABLE, and_64_out, and_65_out);
  or or_13 (RMA_RESET, and_66_out, and_67_out, and_68_out, and_69_out, and_70_out, and_71_out, and_72_out, and_73_out);
  or or_14 (AMA_RESET, and_74_out, and_75_out, and_76_out, and_77_out, and_78_out, and_79_out, and_80_out, and_81_out);
  or or_15 (STEP_RESET, and_82_out, and_83_out, and_84_out, and_85_out, and_86_out, and_87_out, and_88_out, and_89_out, and_90_out);
endmodule
